// Logisim project shiftreg_logisim.circ as structural Verilog: 1 circuit, main circuit main
module main (
);

  J_K_Flip_Flop j_k_ff_1 ();  // open: J, clk, K, Q, Qn, preset, reset
  J_K_Flip_Flop j_k_ff_2 ();  // open: J, clk, K, Q, Qn, preset, reset
  J_K_Flip_Flop j_k_ff_3 ();  // open: J, clk, K, Q, Qn, preset, reset
  J_K_Flip_Flop j_k_ff_4 ();  // open: J, clk, K, Q, Qn, preset, reset
  J_K_Flip_Flop j_k_ff_5 ();  // open: J, clk, K, Q, Qn, preset, reset
  J_K_Flip_Flop j_k_ff_6 ();  // open: J, clk, K, Q, Qn, preset, reset
  J_K_Flip_Flop j_k_ff_7 ();  // open: J, clk, K, Q, Qn, preset, reset
endmodule
